# Fritzing sketch boot_mode_switch (saved by Fritzing 0.9.5d)
stripboards: 1

parts:
  R1 = Resistor [tolerance=±5% resistance=10k package=THT]
  U1 = SWITCH-SPST-2 [package=switch-spst-vertical]

nets:
  N1: R1.Pin_0, U1.P

notes:
  5V
  GND
  MOSI
  10k Resistor
  SPST Switch
  ATMega 16u2 Boot Mode Switch
