# Fritzing sketch breadboard (saved by Fritzing 0.9.3b)
breadboards: 3

parts:
  LCD1 = LCD screen
  Part1 = Arduino Mega 2560 (Rev3)
  S1 = Pushbutton [package="[THT]"]
  R2 = Resistor [tolerance=±5% resistance=220 package=THT]
  LED1 = LED - 5mm [color="Red (633nm)" package="5 mm [THT]"]
  R7 = Resistor [tolerance=±5% resistance=1k package=THT]
  R1 = Trimmer Potentiometer [maximum_resistance=10kΩ package=THT]
  R13 = Resistor [tolerance=±5% resistance=10k package=THT]
  S2 = Pushbutton [package="[THT]"]
  LED2 = LED - 5mm [color="Red (633nm)" package="5 mm [THT]"]
  R14 = Resistor [tolerance=±5% resistance=1k package=THT]
  R15 = Resistor [tolerance=±5% resistance=10k package=THT]
  S3 = Pushbutton [package="[THT]"]
  LED3 = LED - 5mm [color="Red (633nm)" package="5 mm [THT]"]
  R16 = Resistor [tolerance=±5% resistance=1k package=THT]
  R17 = Resistor [tolerance=±5% resistance=10k package=THT]
  S4 = Pushbutton [package="[THT]"]
  LED4 = LED - 5mm [color="Red (633nm)" package="5 mm [THT]"]
  R18 = Resistor [tolerance=±5% resistance=1k package=THT]
  R19 = Resistor [tolerance=±5% resistance=10k package=THT]
  S5 = Pushbutton [package="[THT]"]
  LED5 = LED - 5mm [color="Red (633nm)" package="5 mm [THT]"]
  R20 = Resistor [tolerance=±5% resistance=1k package=THT]
  R21 = Resistor [tolerance=±5% resistance=10k package=THT]
  DIN1 = DIN-5 jack (MIDI) [package=THT]
  R22 = Resistor [tolerance=±5% resistance=220 package=THT]
  R23 = Resistor [tolerance=±5% resistance=220 package=THT]

nets:
  VSS: LCD1.VSS, LCD1.R/W, LCD1.LED-, Part1.GND, R7.Pin_0, R1.leg2, R13.Pin_0, R14.Pin_0, R15.Pin_0, R16.Pin_0, R17.Pin_0, R18.Pin_0, R19.Pin_0, R20.Pin_0, R21.Pin_0, DIN1.2
  VDD: LCD1.VDD, Part1.5V, S1.Pin_1, S1.Pin_2, R2.Pin_0, R1.leg1, S2.Pin_1, S2.Pin_2, S3.Pin_1, S3.Pin_2, S4.Pin_1, S4.Pin_2, S5.Pin_1, S5.Pin_2, R22.Pin_0
  N1: LCD1.V0, R1.wiper
  N2: LCD1.RS, Part1.D7_PWM
  N3: LCD1.E, Part1.D8_PWM
  N4: LCD1.DB4, Part1.D9_PWM
  N5: LCD1.DB5, Part1.D10_PWM
  N6: LCD1.DB6, Part1.D11_PWM
  N7: LCD1.DB7, Part1.D12_PWM
  N8: LCD1.LED+, R2.Pin_1
  N9: Part1.D1_TX0, R23.Pin_0
  N10: Part1.D22, S1.Pin_3, S1.Pin_4, R13.Pin_1
  N11: Part1.D23, S2.Pin_3, S2.Pin_4, R15.Pin_1
  N12: Part1.D24, S3.Pin_3, S3.Pin_4, R17.Pin_1
  N13: Part1.D25, S4.Pin_3, S4.Pin_4, R19.Pin_1
  N14: Part1.D26, S5.Pin_3, S5.Pin_4, R21.Pin_1
  N15: Part1.D38, LED1.anode
  N16: Part1.D39, LED2.anode
  N17: Part1.D40, LED3.anode
  N18: Part1.D41, LED4.anode
  N19: Part1.D42, LED5.anode
  N20: LED1.cathode, R7.Pin_1
  N21: LED2.cathode, R14.Pin_1
  N22: LED3.cathode, R16.Pin_1
  N23: LED4.cathode, R18.Pin_1
  N24: LED5.cathode, R20.Pin_1
  N25: DIN1.5, R23.Pin_1
  N26: DIN1.4, R22.Pin_1
